// Logisim project stage1.circ as structural Verilog: 2 circuits, main circuit interface
module \interface  (
  input  in_1,
  input  in_2,
  input  in_3,
  input  in_4,
  input  in_5,
  input  in_6,
  input  in_7,
  input  in_8,
  input  in_9,
  input  in_10,
  input  in_11,
  input  in_12,
  input  in_13,
  input  in_14,
  input  in_15,
  input  in_16
);

  wire button_1_out, button_4_out;
  wire [7:0] stage1_1_output_pins, stage1_2_output_pins;

  Button button_1 (.out(button_1_out));
  Button button_2 ();  // open: out
  Button button_3 ();  // open: out
  Button button_4 (.out(button_4_out));
  Button button_5 ();  // open: out
  LED led_1 ();  // open: in
  LED led_2 (.in(stage1_1_output_pins[7]));
  LED led_3 (.in(stage1_1_output_pins[6]));
  LED led_4 (.in(stage1_1_output_pins[5]));
  LED led_5 ();  // open: in
  stage1 stage1_1 (
    .input_pins({in_9, in_10, in_11, in_12, in_13, in_14, in_15, in_16}), .Load(button_1_out),
    .Reset(button_4_out), .output_pins(stage1_1_output_pins));
  LED led_6 (.in(stage1_1_output_pins[3]));
  LED led_7 (.in(stage1_1_output_pins[2]));
  LED led_8 ();  // open: in
  LED led_9 (.in(stage1_1_output_pins[1]));
  LED led_10 (.in(stage1_1_output_pins[0]));
  LED led_11 ();  // open: in
  LED led_12 ();  // open: in
  LED led_13 ();  // open: in
  LED led_14 ();  // open: in
  LED led_15 ();  // open: in
  Button button_6 ();  // open: out
  LED led_16 ();  // open: in
  LED led_17 ();  // open: in
  LED led_18 ();  // open: in
  LED led_19 ();  // open: in
  LED led_20 (.in(stage1_2_output_pins[7]));
  LED led_21 (.in(stage1_2_output_pins[6]));
  LED led_22 (.in(stage1_2_output_pins[5]));
  LED led_23 (.in(stage1_2_output_pins[4]));
  LED led_24 (.in(stage1_2_output_pins[3]));
  stage1 stage1_2 (
    .input_pins({in_1, in_2, in_3, in_4, in_5, in_6, in_7, in_8}), .Load(button_1_out), .Reset(button_4_out),
    .output_pins(stage1_2_output_pins));
  LED led_25 (.in(stage1_2_output_pins[2]));
  LED led_26 (.in(stage1_2_output_pins[1]));
  LED led_27 (.in(stage1_2_output_pins[0]));

  // Notes on the sheet:
  //   Load
  //   Add
  //   Subtract
  //   Reset
  //   +/-
  //   +/-
  //   Input A Display
  //   +/-
  //   8 bit Binary Calculator
  //   Input A
  //   Output
  //   +/-
  //   +/-
  //   Input B
  //   Input B Display
endmodule

module stage1 (
  input  [7:0] input_pins,
  input  Load,
  input  Reset,
  output [7:0] output_pins
);

  D_Flip_Flop d_ff_1 (.D(input_pins[0]), .clk(Load), .Q(output_pins[0]), .reset(Reset));  // open: Qn, preset
  D_Flip_Flop d_ff_2 (.D(input_pins[1]), .clk(Load), .Q(output_pins[1]), .reset(Reset));  // open: Qn, preset
  D_Flip_Flop d_ff_3 (.D(input_pins[2]), .clk(Load), .Q(output_pins[2]), .reset(Reset));  // open: Qn, preset
  D_Flip_Flop d_ff_4 (.D(input_pins[3]), .clk(Load), .Q(output_pins[3]), .reset(Reset));  // open: Qn, preset
  D_Flip_Flop d_ff_5 (.D(input_pins[4]), .clk(Load), .Q(output_pins[4]), .reset(Reset));  // open: Qn, preset
  D_Flip_Flop d_ff_6 (.D(input_pins[5]), .clk(Load), .Q(output_pins[5]), .reset(Reset));  // open: Qn, preset
  D_Flip_Flop d_ff_7 (.D(input_pins[6]), .clk(Load), .Q(output_pins[6]), .reset(Reset));  // open: Qn, preset
  D_Flip_Flop d_ff_8 (.D(input_pins[7]), .clk(Load), .Q(output_pins[7]), .reset(Reset));  // open: Qn, preset
endmodule
