// Logisim project full_adder.circ as structural Verilog: 1 circuit, main circuit main
module main (
  input  in_1,
  input  in_2,
  input  in_3
);

  wire and_1_out, and_2_out, xor_1_out;

  xor xor_1 (xor_1_out, in_1, in_2);
  and and_1 (and_1_out, xor_1_out, in_3);
  and and_2 (and_2_out, in_2, in_1);
  // XOR_Gate xor_2 has open pins: in0=xor_1_out, in1=in_3, out=open
  // OR_Gate or_1 has open pins: in0=and_1_out, in1=and_2_out, out=open
endmodule
