// Logisim project 4_bit_adder.circ as structural Verilog: 1 circuit, main circuit main
module main (
  input  A2,
  input  B2,
  input  A1,
  input  B1,
  input  A0,
  input  B0,
  input  A3,
  input  B3
);

  wire and_1_out, and_2_out, and_3_out, and_4_out, and_5_out, and_6_out, and_7_out, or_1_out, or_2_out,
       or_3_out, xor_1_out, xor_2_out, xor_3_out, xor_4_out, xor_5_out, xor_6_out, xor_7_out;

  and and_1 (and_1_out, A3, B3);
  and and_2 (and_2_out, xor_1_out, or_2_out);
  or or_1 (or_1_out, and_1_out, and_2_out);
  LED led_1 (.in(or_1_out));
  xor xor_1 (xor_1_out, A3, B3);
  xor xor_2 (xor_2_out, xor_1_out, or_2_out);
  LED led_2 (.in(xor_2_out));
  and and_3 (and_3_out, A2, B2);
  or or_2 (or_2_out, and_3_out, and_4_out);
  xor xor_3 (xor_3_out, A2, B2);
  and and_4 (and_4_out, xor_3_out, or_3_out);
  xor xor_4 (xor_4_out, xor_3_out, or_3_out);
  LED led_3 (.in(xor_4_out));
  and and_5 (and_5_out, A1, B1);
  and and_6 (and_6_out, xor_5_out, and_7_out);
  or or_3 (or_3_out, and_5_out, and_6_out);
  xor xor_5 (xor_5_out, A1, B1);
  xor xor_6 (xor_6_out, xor_5_out, and_7_out);
  LED led_4 (.in(xor_6_out));
  and and_7 (and_7_out, A0, B0);
  xor xor_7 (xor_7_out, A0, B0);
  LED led_5 (.in(xor_7_out));
endmodule
