// Logisim project full_adder.circ as structural Verilog: 1 circuit, main circuit main
module main (
  input  input_1,
  input  input_2,
  input  carry_in
);

  wire and_1_out, and_2_out, or_1_out, xor_1_out, xor_2_out;

  xor xor_1 (xor_1_out, input_1, input_2);
  xor xor_2 (xor_2_out, xor_1_out, carry_in);
  and and_1 (and_1_out, xor_1_out, carry_in);
  and and_2 (and_2_out, input_2, input_1);
  LED led_1 (.in(xor_2_out));
  or or_1 (or_1_out, and_1_out, and_2_out);
  LED led_2 (.in(or_1_out));

  // Notes on the sheet:
  //   Sum Output
  //   Carry Output
endmodule
